# Fritzing sketch lnshield_sample (saved by Fritzing 0.9.3b)
breadboards: 1
perfboards: 1

parts:
  パーツ1 = Arduino Uno (Rev3)
  S1 = Pushbutton [package="[THT]"]
  LED1 = LED - 5mm [color="Red (633nm)" package="5 mm [THT]"]
  R1 = Resistor [tolerance=±5% resistance=220 package=THT]

nets:
  N1: パーツ1.GND, S1.Pin_3, S1.Pin_4, LED1.cathode
  N2: パーツ1.D5_PWM, R1.Pin_1
  N3: パーツ1.D6_PWM, S1.Pin_1, S1.Pin_2
  N4: LED1.anode, R1.Pin_0
